# Fritzing sketch circuito_encoder_raspberry (saved by Fritzing 0.9.3b)

parts:
  DC_Mot_Enc2 = DC Motor with two-phase hall-encoder [part_number=VT-E-G25A-06-177E]
  Part2 = Adafruit T-Cobbler Plus [part_number="Adafruit #1989 and #2028"]

nets:
  N1: DC_Mot_Enc2.pin3, Part2.GPIO5
  N2: DC_Mot_Enc2.pin4, Part2.+3.3V
  N3: DC_Mot_Enc2.pin5, Part2.GND
  N4: DC_Mot_Enc2.pin6, Part2.GPIO6

notes:
  Motor de 12 v
  Adaptador tipo T de raspberry

custom parts:
  Adafruit T-Cobbler Plus: The Raspberry Pi has landed on the Maker World like a 40-GPIO pinned, quad-USB ported, credit card sized bomb of DIY joy. And while you can use most of our great Model B accessories by hooking up our downgrade cable, its probably a good time to upgrade your set up and accessorize using all of the 40 pins. That's why we now carry the Assembled Adafruit Pi T-Cobbler Plus - Breakout + Cable for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
