# Fritzing sketch circuito_motor_dc_encoder_L298N (saved by Fritzing 0.9.3b)

parts:
  S1 = H-Bridge with L298N
  DC_Mot_Enc1 = DC Motor with two-phase hall-encoder [part_number=VT-E-G25A-06-177E]
  Part1 = Adafruit T-Cobbler Plus [part_number="Adafruit #1989 and #2028"]
  J1 = 2.1mm Barrel Jack with Terminal Block

nets:
  N1: S1.12V, J1.POS
  N2: S1.GND, J1.NEG
  N3: S1.ENA, Part1.GPIO25, Part1.CE0
  N4: S1.IN1, Part1.GPIO23
  N5: S1.IN2, DC_Mot_Enc1.pin5, Part1.GND, Part1.GPIO24
  N6: S1.M1-01, DC_Mot_Enc1.pin2
  N7: S1.M1-02, DC_Mot_Enc1.pin1
  N8: DC_Mot_Enc1.pin3, Part1.GPIO5
  N9: DC_Mot_Enc1.pin4, Part1.+3.3V
  N10: DC_Mot_Enc1.pin6, Part1.GPIO6

notes:
  Motor de 12 v
  Adaptador de corriente 12v

custom parts:
  H-Bridge with L298N: h-bridge
  Adafruit T-Cobbler Plus: The Raspberry Pi has landed on the Maker World like a 40-GPIO pinned, quad-USB ported, credit card sized bomb of DIY joy. And while you can use most of our great Model B accessories by hooking up our downgrade cable, its probably a good time to upgrade your set up and accessorize using all of the 40 pins. That's why we now carry the Assembled Adafruit Pi T-Cobbler Plus - Breakout + Cable for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
