# Fritzing sketch circuito_motor_encoder_L298N_pantalla (saved by Fritzing 0.9.3b)

parts:
  J2 = 2.1mm Barrel Jack with Terminal Block
  S2 = H-Bridge with L298N
  DC_Mot_Enc2 = DC Motor with two-phase hall-encoder [part_number=VT-E-G25A-06-177E]
  Part2 = Adafruit T-Cobbler Plus [part_number="Adafruit #1989 and #2028"]
  o1 = Module display OLED I2C 128x64 SSD1306 [package=THT]

nets:
  N1: J2.POS, S2.12V
  N2: J2.NEG, S2.GND
  N3: S2.ENA, Part2.GPIO25, Part2.CE0
  N4: S2.IN1, Part2.GPIO23
  GND: S2.IN2, DC_Mot_Enc2.pin5, Part2.GND, Part2.GPIO24, o1.GND
  N5: S2.M1-01, DC_Mot_Enc2.pin2
  N6: S2.M1-02, DC_Mot_Enc2.pin1
  N7: DC_Mot_Enc2.pin3, Part2.GPIO5
  +3.3V: DC_Mot_Enc2.pin4, Part2.+3.3V, o1.VCC
  N8: DC_Mot_Enc2.pin6, Part2.GPIO6
  N9: Part2.SDA, o1.SDA
  N10: Part2.SCL, o1.SCL

notes:
  Motor de 12 v
  Adaptador de corriente 12v

custom parts:
  H-Bridge with L298N: h-bridge
  Adafruit T-Cobbler Plus: The Raspberry Pi has landed on the Maker World like a 40-GPIO pinned, quad-USB ported, credit card sized bomb of DIY joy. And while you can use most of our great Model B accessories by hooking up our downgrade cable, its probably a good time to upgrade your set up and accessorize using all of the 40 pins. That's why we now carry the Assembled Adafruit Pi T-Cobbler Plus - Breakout + Cable for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
  Module display OLED I2C 128x64 SSD1306: Ecran OLED I2C SSD163 de 128x64 avec connexion I2C
