# Fritzing sketch circuito_raspberry_pantalla_oled (saved by Fritzing 0.9.3b)

parts:
  Part3 = Adafruit T-Cobbler Plus [part_number="Adafruit #1989 and #2028"]
  o2 = Module display OLED I2C 128x64 SSD1306 [package=THT]

nets:
  +3.3V: Part3.+3.3V, o2.VCC
  N1: Part3.SDA, o2.SDA
  N2: Part3.SCL, o2.SCL
  GND: Part3.GND, o2.GND

custom parts:
  Adafruit T-Cobbler Plus: The Raspberry Pi has landed on the Maker World like a 40-GPIO pinned, quad-USB ported, credit card sized bomb of DIY joy. And while you can use most of our great Model B accessories by hooking up our downgrade cable, its probably a good time to upgrade your set up and accessorize using all of the 40 pins. That's why we now carry the Assembled Adafruit Pi T-Cobbler Plus - Breakout + Cable for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
  Module display OLED I2C 128x64 SSD1306: Ecran OLED I2C SSD163 de 128x64 avec connexion I2C
